# Fritzing sketch circuit (saved by Fritzing 0.9.3b)
breadboards: 1

parts:
  Part2 = 16-Channel 12-bit PWM Servo Driver - I2C [part_number=815]
  J4 = Basic Servo
  J7 = Basic Servo
  Raspberry_Pi_2 = Raspberry Pi 3 [part_number=RPI-3-V1.2]
  S2 = Pushbutton [package="[THT]"]
  R2 = Resistor [tolerance=±5% resistance=10k package="0402 [SMD]"]
  R3 = Resistor [tolerance=±5% resistance=470 package="0402 [SMD]"]
  LED2 = smd LED [color="Red (633nm)" package="1206 [SMD]"]
  J6 = Basic Servo
  Power_plug1 = Power plug

nets:
  N1: Part2.PWRIN, Power_plug1.VCC
  GND: Part2.GND, J4.gnd, J7.gnd, Raspberry_Pi_2.GND, S2.Pin_1, S2.Pin_2, LED2.cathode, J6.gnd, Power_plug1.GND
  3V3: Part2.VCC, Raspberry_Pi_2.3v3, Raspberry_Pi_2.3V3
  N2: Part2.SDA, Raspberry_Pi_2.ID_SD
  N3: Part2.SCL, Raspberry_Pi_2.ID_SC
  N4: Part2.PWM14, J4.pulse
  VCC: Part2.5.0V, J4.vcc, J7.vcc, J6.vcc
  N5: Part2.PWM12, J7.pulse
  N6: Part2.PWM8, J6.pulse
  N7: Raspberry_Pi_2.GPIO6, R3.Pin_0
  N8: Raspberry_Pi_2.GPIO21, S2.Pin_3, S2.Pin_4, R2.Pin_1
  N9: Raspberry_Pi_2.5V, R2.Pin_0
  N10: R3.Pin_1, LED2.anode

custom parts:
  16-Channel 12-bit PWM Servo Driver - I2C: You want to make a cool robot, maybe a hexapod walker, or maybe just a piece of art with a lot of moving parts. Or maybe you want to drive a lot of LEDs with precise PWM output. Using only two pins, control 16 free-running PWM outputs! You can even chain up 62 breakouts to control up to 992 PWM outputs.
